// Logisim project adh0.circ as structural Verilog
module ALU (
  input  [2:0] op,
  input  [7:0] x,
  input  [7:0] y
);

  wire n7404_1_pin2, n7404_1_pin4, n7404_1_pin6, n7404_1_pin8, n7404_1_pin10, n7404_1_pin12, n7432_2_pin8,
       n7442_1_pin2, n7442_1_pin3, n7442_1_pin4, n7442_1_pin5, n7442_1_pin6, n7442_1_pin7, n7442_1_pin12,
       n7486_1_pin2, n74283_1_pin7;
  wire [7:0] adders_pin4, ands_pin6, n7432_1_pin3, n7486_1_pin11, n7486_2_pin3;

  _7442 u_7442_1 (
    .pin2(n7442_1_pin2), .pin3(n7442_1_pin3), .pin4(n7442_1_pin4), .pin5(n7442_1_pin5), .pin6(n7442_1_pin6),
    .pin7(n7442_1_pin7), .pin15(op[0]), .pin14(op[1]), .pin13(op[2]), .pin12(n7442_1_pin12));  // open: pin1, pin11, pin10, pin9
  _7404 u_7404_1 (
    .pin1(n7442_1_pin5), .pin2(n7404_1_pin2), .pin3(n7442_1_pin6), .pin4(n7404_1_pin4), .pin5(n7442_1_pin7),
    .pin6(n7404_1_pin6), .pin13(n7442_1_pin2), .pin12(n7404_1_pin12), .pin11(n7442_1_pin3),
    .pin10(n7404_1_pin10), .pin9(n7442_1_pin4), .pin8(n7404_1_pin8));
  _7408 u_7408_1 (
    .pin1(y[5]), .pin2(x[5]), .pin3(ands_pin6[5]), .pin4(y[4]), .pin5(x[4]), .pin6(ands_pin6[4]),
    .pin13(y[7]), .pin12(x[7]), .pin11(ands_pin6[7]), .pin10(y[6]), .pin9(x[6]), .pin8(ands_pin6[6]));
  _7432 u_7432_1 (
    .pin1(x[0]), .pin2(y[0]), .pin3(n7432_1_pin3[0]), .pin4(x[1]), .pin5(y[1]), .pin6(n7432_1_pin3[1]),
    .pin13(x[7]), .pin12(y[7]), .pin11(n7432_1_pin3[7]), .pin10(x[6]), .pin9(y[6]), .pin8(n7432_1_pin3[6]));
  _7486 u_7486_1 (
    .pin1(y[4]), .pin2(n7486_1_pin2), .pin3(n7486_1_pin11[4]), .pin4(y[5]), .pin5(n7486_1_pin2),
    .pin6(n7486_1_pin11[5]), .pin13(y[0]), .pin12(n7486_1_pin2), .pin11(n7486_1_pin11[0]), .pin10(y[1]),
    .pin9(n7486_1_pin2), .pin8(n7486_1_pin11[1]));
  _7432 u_7432_2 (
    .pin13(n7404_1_pin8), .pin12(n7404_1_pin10), .pin11(n7486_1_pin2), .pin10(n7404_1_pin10),
    .pin9(n7404_1_pin12), .pin8(n7432_2_pin8));  // open: pin1, pin2, pin3, pin4, pin5, pin6
  _7408 ands (
    .pin1(y[1]), .pin2(x[1]), .pin3(ands_pin6[1]), .pin4(y[0]), .pin5(x[0]), .pin6(ands_pin6[0]),
    .pin13(y[3]), .pin12(x[3]), .pin11(ands_pin6[3]), .pin10(y[2]), .pin9(x[2]), .pin8(ands_pin6[2]));
  _7432 ors (
    .pin1(x[4]), .pin2(y[4]), .pin3(n7432_1_pin3[4]), .pin4(x[5]), .pin5(y[5]), .pin6(n7432_1_pin3[5]),
    .pin13(x[3]), .pin12(y[3]), .pin11(n7432_1_pin3[3]), .pin10(x[2]), .pin9(y[2]), .pin8(n7432_1_pin3[2]));
  _7486 inv (
    .pin1(y[6]), .pin2(n7486_1_pin2), .pin3(n7486_1_pin11[6]), .pin4(y[7]), .pin5(n7486_1_pin2),
    .pin6(n7486_1_pin11[7]), .pin13(y[2]), .pin12(n7486_1_pin2), .pin11(n7486_1_pin11[2]), .pin10(y[3]),
    .pin9(n7486_1_pin2), .pin8(n7486_1_pin11[3]));
  _7404 #(.ShowInternalStructure("true")) u_7404_2 ();  // open: pin1, pin2, pin3, pin4, pin5, pin6, pin13, pin12, pin11, pin10, pin9, pin8
  _7486 #(.ShowInternalStructure("true")) u_7486_2 (
    .pin1(x[0]), .pin2(y[0]), .pin3(n7486_2_pin3[0]), .pin4(x[1]), .pin5(y[1]), .pin6(n7486_2_pin3[1]),
    .pin13(x[7]), .pin12(y[7]), .pin11(n7486_2_pin3[7]), .pin10(x[6]), .pin9(y[6]), .pin8(n7486_2_pin3[6]));
  _74283 u_74283_1 (
    .pin1(adders_pin4[5]), .pin2(n7486_1_pin11[5]), .pin3(x[5]), .pin4(adders_pin4[4]), .pin5(x[4]),
    .pin6(n7486_1_pin11[4]), .pin7(n74283_1_pin7), .pin15(n7486_1_pin11[6]), .pin14(x[6]),
    .pin13(adders_pin4[6]), .pin12(x[7]), .pin11(n7486_1_pin11[7]), .pin10(adders_pin4[7]));  // open: pin9
  _7404 #(.ShowInternalStructure("true")) u_7404_3 ();  // open: pin1, pin2, pin3, pin4, pin5, pin6, pin13, pin12, pin11, pin10, pin9, pin8
  _7486 #(.ShowInternalStructure("true")) u_7486_3 (
    .pin1(x[4]), .pin2(y[4]), .pin3(n7486_2_pin3[4]), .pin4(x[5]), .pin5(y[5]), .pin6(n7486_2_pin3[5]),
    .pin13(x[3]), .pin12(y[3]), .pin11(n7486_2_pin3[3]), .pin10(x[2]), .pin9(y[2]), .pin8(n7486_2_pin3[2]));
  _74283 adders (
    .pin1(adders_pin4[1]), .pin2(n7486_1_pin11[1]), .pin3(x[1]), .pin4(adders_pin4[0]), .pin5(x[0]),
    .pin6(n7486_1_pin11[0]), .pin7(n7432_2_pin8), .pin15(n7486_1_pin11[2]), .pin14(x[2]),
    .pin13(adders_pin4[2]), .pin12(x[3]), .pin11(n7486_1_pin11[3]), .pin10(adders_pin4[3]),
    .pin9(n74283_1_pin7));
  // also tied to GND on the sheet: n7442_1_pin12
endmodule
